// Logisim project ripple.circ as structural Verilog: 3 circuits, main circuit main
module fulladder (
  input  in_1
);

  main main_1 ();  // open: in_1, in_2, out_3, out_4
  main main_2 ();  // open: in_1, in_2, out_3, out_4
  main main_3 ();  // open: in_1, in_2, out_3, out_4
endmodule

module main (
  input  in_1,
  input  in_2,
  output out_3,
  output out_4
);

  wire and_1_out, and_2_out, xor_1_out;

  and and_1 (and_1_out, in_1, in_1);
  xor xor_1 (xor_1_out, in_1, in_1);
  and and_2 (and_2_out, xor_1_out, in_2);
  xor xor_2 (out_4, and_2_out, and_1_out);
  xor xor_3 (out_3, xor_1_out, in_2);
endmodule

module full (
);

  main main_1 ();  // open: in_1, in_2, out_3, out_4
endmodule
